// Logisim project Organización de computadores.circ as structural Verilog: 19 circuits, main circuit Mux
module Mux (
  input  A,
  input  B,
  input  Sel,
  output out
);

  wire And1_out, And1A_out, And2_out, And2A_out, And3_out, And3A_out, And4_out, notA_out, notB_out,
       notSel_out, Or1_2_out, Or1_out;

  not notA (notA_out, A);
  not notB (notB_out, B);
  not notSel (notSel_out, Sel);
  and And1A (And1A_out, notA_out, B);
  and And2A (And2A_out, A, notB_out);
  and And3A (And3A_out, B, A);
  and And1 (And1_out, And1A_out, Sel);
  and And2 (And2_out, And2A_out, notSel_out);
  and And3 (And3_out, And3A_out, notSel_out);
  and And4 (And4_out, And3A_out, Sel);
  or Or1 (Or1_out, And1_out, And2_out);
  or Or1_2 (Or1_2_out, And3_out, And4_out);
  or or_1 (out, Or1_out, Or1_2_out);
endmodule

module Dmux (
  input  In,
  input  Sel,
  output A,
  output B
);

  wire notSel_out;

  not notSel (notSel_out, Sel);
  and And1 (A, In, notSel_out);
  and And2 (B, In, Sel);
endmodule

module Not16 (
  input  [15:0] in_1,
  output [15:0] out_2
);

  assign out_2 = ~in_1;  // NOT_Gate not_1, 16 bits wide
endmodule

module DFF (
  input  Clock,
  input  in_2,
  input  in_3,
  output out_4
);

  wire multiplexer_1_out;

  Multiplexer multiplexer_1 (.in0(out_4), .in1(in_3), .out(multiplexer_1_out), .sel(in_2));  // open: en
  D_Flip_Flop d_ff_1 (.clk(Clock), .D(multiplexer_1_out), .Q(out_4));  // open: Qn, preset, en, reset
endmodule

// IN
module Register16 (
  input  Load,
  input  [15:0] in_2,
  output [15:0] out_3
);

  wire Clock;

  Clock clock_1 (.out(Clock));
  DFF dff_1 (.in_2(Load), .in_3(in_2[0]), .Clock(Clock), .out_4(out_3[0]));
  DFF dff_2 (.in_2(Load), .in_3(in_2[1]), .Clock(Clock), .out_4(out_3[1]));
  DFF dff_3 (.in_2(Load), .in_3(in_2[2]), .Clock(Clock), .out_4(out_3[2]));
  DFF dff_4 (.in_2(Load), .in_3(in_2[3]), .Clock(Clock), .out_4(out_3[3]));
  DFF dff_5 (.in_2(Load), .in_3(in_2[4]), .Clock(Clock), .out_4(out_3[4]));
  DFF dff_6 (.in_2(Load), .in_3(in_2[5]), .Clock(Clock), .out_4(out_3[5]));
  DFF dff_7 (.in_2(Load), .in_3(in_2[6]), .Clock(Clock), .out_4(out_3[6]));
  DFF dff_8 (.in_2(Load), .in_3(in_2[7]), .Clock(Clock), .out_4(out_3[7]));
  DFF dff_9 (.in_2(Load), .in_3(in_2[8]), .Clock(Clock), .out_4(out_3[8]));
  DFF dff_10 (.in_2(Load), .in_3(in_2[9]), .Clock(Clock), .out_4(out_3[9]));
  DFF dff_11 (.in_2(Load), .in_3(in_2[10]), .Clock(Clock), .out_4(out_3[10]));
  DFF dff_12 (.in_2(Load), .in_3(in_2[11]), .Clock(Clock), .out_4(out_3[11]));
  DFF dff_13 (.in_2(Load), .in_3(in_2[12]), .Clock(Clock), .out_4(out_3[12]));
  DFF dff_14 (.in_2(Load), .in_3(in_2[13]), .Clock(Clock), .out_4(out_3[13]));
  DFF dff_15 (.in_2(Load), .in_3(in_2[14]), .Clock(Clock), .out_4(out_3[14]));
  DFF dff_16 (.in_2(Load), .in_3(in_2[15]), .Clock(Clock), .out_4(out_3[15]));
endmodule

module And16 (
  input  [15:0] IN,
  input  [15:0] IN_2,
  output [15:0] OUT
);

  assign OUT = IN & IN_2;  // AND_Gate AND, 16 bits wide
endmodule

module Or16 (
  input  [15:0] IN,
  input  [15:0] IN_2,
  output [15:0] OUT
);

  assign OUT = IN | IN_2;  // OR_Gate or_1, 16 bits wide
endmodule

module Xor16 (
  input  [15:0] IN,
  input  [15:0] IN_2,
  output [15:0] OUT
);

  assign OUT = IN ^ IN_2;  // XOR_Gate xor_1, 16 bits wide
endmodule

module Or8way (
  input  in_1,
  input  in_2,
  input  in_3,
  input  in_4,
  input  in_5,
  input  in_6,
  input  in_7,
  input  in_8,
  output out_9
);

  or or_1 (out_9, in_1, in_2, in_3, in_4, in_5, in_6, in_7, in_8);
endmodule

module Mux4Way16 (
  input  [1:0] Sel_2,
  input  [15:0] A,
  input  [15:0] B,
  input  [15:0] C,
  input  [15:0] D,
  output [15:0] out_6
);

  wire [15:0] MUX16AB_out_4, MUX16CD_out_4;

  Mux16 MUX16AB (.Sel(Sel_2[0]), .A(A), .B(B), .out_4(MUX16AB_out_4));
  Mux16 MUX16CD (.Sel(Sel_2[0]), .A(C), .B(D), .out_4(MUX16CD_out_4));
  Mux16 MUX_MUX1_2 (.Sel(Sel_2[1]), .A(MUX16AB_out_4), .B(MUX16CD_out_4), .out_4(out_6));
endmodule

module Mux16 (
  input  Sel,
  input  [15:0] A,
  input  [15:0] B,
  output [15:0] out_4
);

  wire not_1_out;
  wire [15:0] And_A_Nsel_out, And_B_Sel_out, bit_extender_1_out, bit_extender_2_out;

  not not_1 (not_1_out, Sel);
  assign bit_extender_1_out = {{15{not_1_out}}, not_1_out};  // Bit_Extender bit_extender_1
  assign bit_extender_2_out = {{15{Sel}}, Sel};  // Bit_Extender bit_extender_2
  assign And_A_Nsel_out = bit_extender_1_out & A;  // AND_Gate And_A_Nsel, 16 bits wide
  assign And_B_Sel_out = B & bit_extender_2_out;  // AND_Gate And_B_Sel, 16 bits wide
  Or16 Or16 (.IN(And_A_Nsel_out), .IN_2(And_B_Sel_out), .OUT(out_4));
endmodule

module Mux8Way16 (
  input  [2:0] Sel_2,
  input  [15:0] A,
  input  [15:0] E,
  input  [15:0] B,
  input  [15:0] F,
  input  [15:0] C,
  input  [15:0] G,
  input  [15:0] D,
  input  [15:0] H,
  output [15:0] out_10
);

  wire [15:0] Mux_ABCD_2_out_6, Mux_ABCD_out_6;

  Mux4Way16 Mux_ABCD (.Sel_2(Sel_2[1:0]), .A(A), .B(B), .C(C), .D(D), .out_6(Mux_ABCD_out_6));
  Mux16 mux16_1 (.Sel(Sel_2[2]), .A(Mux_ABCD_out_6), .B(Mux_ABCD_2_out_6), .out_4(out_10));
  Mux4Way16 Mux_ABCD_2 (.Sel_2(Sel_2[1:0]), .A(E), .B(F), .C(G), .D(H), .out_6(Mux_ABCD_2_out_6));
endmodule

module Dmux4way (
  input  [1:0] Sel,
  input  in,
  output out_3,
  output out_4,
  output out_5,
  output out_6
);

  wire dmux_1_a, dmux_1_b;

  Dmux dmux_1 (.In(in), .Sel(Sel[1]), .A(dmux_1_a), .B(dmux_1_b));
  Dmux dmux_2 (.In(dmux_1_a), .Sel(Sel[0]), .A(out_3), .B(out_4));
  Dmux dmux_3 (.In(dmux_1_b), .Sel(Sel[0]), .A(out_5), .B(out_6));
endmodule

module Dmux8Way (
  input  [2:0] Sel,
  input  IN,
  output out_3,
  output out_4,
  output out_5,
  output out_6,
  output out_7,
  output out_8,
  output out_9,
  output out_10
);

  wire dmux_1_a, dmux_1_b;

  Dmux dmux_1 (.In(IN), .Sel(Sel[2]), .A(dmux_1_a), .B(dmux_1_b));
  Dmux4way dmux4way_1 (.Sel(Sel[1:0]), .in(dmux_1_a), .out_3(out_3), .out_4(out_4), .out_5(out_5), .out_6(out_6));
  Dmux4way dmux4way_2 (.Sel(Sel[1:0]), .in(dmux_1_b), .out_3(out_7), .out_4(out_8), .out_5(out_9), .out_6(out_10));
endmodule

module HalfAdder (
  input  A,
  input  B,
  output SUM,
  output Carry
);

  xor xor_1 (SUM, A, B);
  and and_1 (Carry, A, B);
endmodule

module FullAdder (
  input  A,
  input  B,
  input  C,
  output Sum,
  output Carry
);

  wire and_1_out, HalfAdder_carry, HalfAdder_sum;

  HalfAdder HalfAdder (.A(A), .B(B), .SUM(HalfAdder_sum), .Carry(HalfAdder_carry));
  xor xor_1 (Sum, HalfAdder_sum, C);
  and and_1 (and_1_out, HalfAdder_sum, C);
  or or_1 (Carry, HalfAdder_carry, and_1_out);
endmodule

module HalfAdder16 (
  input  [15:0] A,
  input  [15:0] B,
  output [15:0] Sum,
  output [15:0] Carry
);

  assign Sum = A ^ B;  // XOR_Gate xor_1, 16 bits wide
  assign Carry = A & B;  // AND_Gate and_1, 16 bits wide
endmodule

module FullAdder16 (
  input  [15:0] A,
  input  [15:0] B,
  input  [15:0] C,
  output [15:0] Sum,
  output [15:0] Carry
);

  wire [15:0] HalfAdder16_2_carry, HalfAdder16_carry, HalfAdder16_sum;

  HalfAdder16 HalfAdder16 (.A(A), .B(B), .Sum(HalfAdder16_sum), .Carry(HalfAdder16_carry));
  HalfAdder16 HalfAdder16_2 (.A(HalfAdder16_sum), .B(C), .Sum(Sum), .Carry(HalfAdder16_2_carry));
  Or16 OR16 (.IN(HalfAdder16_carry), .IN_2(HalfAdder16_2_carry), .OUT(Carry));
endmodule

module Add16 (
  input  [15:0] A,
  input  [15:0] B,
  output [15:0] out_3,
  output Carry
);

  wire FullAdder1_2_carry, FullAdder1_3_carry, FullAdder1_carry, FullAdder2_2_carry, FullAdder2_carry,
       FullAdder3_2_carry, FullAdder3_carry, FullAdder4_2_carry, FullAdder4_carry, FullAdder5_2_carry,
       FullAdder5_carry, FullAdder6_2_carry, FullAdder6_carry, FullAdder7_carry, Halfadder_carry;

  HalfAdder Halfadder (.A(A[0]), .B(B[0]), .SUM(out_3[0]), .Carry(Halfadder_carry));
  FullAdder FullAdder4 (.A(A[4]), .B(B[4]), .C(FullAdder3_carry), .Sum(out_3[4]), .Carry(FullAdder4_carry));
  FullAdder FullAdder1 (.A(A[8]), .B(B[8]), .C(FullAdder7_carry), .Sum(out_3[8]), .Carry(FullAdder1_carry));
  FullAdder FullAdder4_2 (.A(A[12]), .B(B[12]), .C(FullAdder3_2_carry), .Sum(out_3[12]), .Carry(FullAdder4_2_carry));
  FullAdder FullAdder1_2 (.A(A[1]), .B(B[1]), .C(Halfadder_carry), .Sum(out_3[1]), .Carry(FullAdder1_2_carry));
  FullAdder FullAdder5 (.A(A[5]), .B(B[5]), .C(FullAdder4_carry), .Sum(out_3[5]), .Carry(FullAdder5_carry));
  FullAdder FullAdder1_3 (.A(A[9]), .B(B[9]), .C(FullAdder1_carry), .Sum(out_3[9]), .Carry(FullAdder1_3_carry));
  FullAdder FullAdder5_2 (.A(A[13]), .B(B[13]), .C(FullAdder4_2_carry), .Sum(out_3[13]), .Carry(FullAdder5_2_carry));
  FullAdder FullAdder2 (.A(A[2]), .B(B[2]), .C(FullAdder1_2_carry), .Sum(out_3[2]), .Carry(FullAdder2_carry));
  FullAdder FullAdder6 (.A(A[6]), .B(B[6]), .C(FullAdder5_carry), .Sum(out_3[6]), .Carry(FullAdder6_carry));
  FullAdder FullAdder3 (.A(A[3]), .B(B[3]), .C(FullAdder2_carry), .Sum(out_3[3]), .Carry(FullAdder3_carry));
  FullAdder FullAdder7 (.A(A[7]), .B(B[7]), .C(FullAdder6_carry), .Sum(out_3[7]), .Carry(FullAdder7_carry));
  FullAdder FullAdder2_2 (.A(A[10]), .B(B[10]), .C(FullAdder1_3_carry), .Sum(out_3[10]), .Carry(FullAdder2_2_carry));
  FullAdder FullAdder6_2 (.A(A[14]), .B(B[14]), .C(FullAdder5_2_carry), .Sum(out_3[14]), .Carry(FullAdder6_2_carry));
  FullAdder FullAdder3_2 (.A(A[11]), .B(B[11]), .C(FullAdder2_2_carry), .Sum(out_3[11]), .Carry(FullAdder3_2_carry));
  FullAdder FullAdder7_2 (.A(A[15]), .B(B[15]), .C(FullAdder6_2_carry), .Sum(out_3[15]), .Carry(Carry));
endmodule
